# Fritzing sketch esp (saved by Fritzing 0.9.1b)
circuit board: 8.46667cm x 5.64444cm
breadboards: 1

parts:
  MOD-WIFI-ESP8266-DEV1 = Olimex ESP8266 DEV
  Part1 = FTDI Basic Programmer
  R1 = Resistor [tolerance=±5% resistance=3.3 package=THT]
  PSU1 = Adjustable Breadboard Power Supply
  R2 = Resistor [tolerance=±5% resistance=1.5 package=THT]
  Flash_mode = Pushbutton [package="[SMD]"]
  Reset = Pushbutton [package="[SMD]"]
  LED1 = LED - 3mm [color="Green (565nm)" package="3 mm [THT]"]
  S1 = Pushbutton [package="[THT]"]

nets:
  N1: MOD-WIFI-ESP8266-DEV1.3.3V, R1.Pin_1, PSU1.Vout+, S1.Pin_3, S1.Pin_4
  GND: MOD-WIFI-ESP8266-DEV1.GND, Part1.GND, PSU1.Vout-, R2.Pin_1, Flash_mode.Pin_1, Flash_mode.Pin_2, Reset.Pin_3, Reset.Pin_4, LED1.cathode
  N2: MOD-WIFI-ESP8266-DEV1.GPIO1, Part1.RXI
  N3: MOD-WIFI-ESP8266-DEV1.GPIO3, Part1.TXO
  N4: MOD-WIFI-ESP8266-DEV1.ADC, R1.Pin_0, R2.Pin_0
  N5: MOD-WIFI-ESP8266-DEV1.RSTB, MOD-WIFI-ESP8266-DEV1.GPIO16, Reset.Pin_1, Reset.Pin_2
  N6: MOD-WIFI-ESP8266-DEV1.GPIO15, S1.Pin_1, S1.Pin_2
  N7: MOD-WIFI-ESP8266-DEV1.GPIO0, Flash_mode.Pin_3, Flash_mode.Pin_4
  N8: MOD-WIFI-ESP8266-DEV1.GPIO4, LED1.anode

custom parts:
  Olimex ESP8266 DEV: MOD-WIFI-ESP8266-DEV is the ultimate development board for ESP8266 with all GPIOs and resources exposed, can be soldered to PCB or used with breadboard and UEXT. Small U.FL connector is provided for external antenna connection. ESP8266 is very highly integrated SOC which includes Xtensa LX106 core processor, RAM, RF front end and allow WIFI TCP-IP stack to be implemented on board with just few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
